// Logisim project Carry Lookahead Adder.circ as structural Verilog: 5 circuits, main circuit CLA
module CLA (
  input  Cin,
  input  [3:0] A,
  input  [3:0] B,
  output Cout,
  output [3:0] S
);

  wire bcd_to_7_segment_decoder_1_p1, logic_block_1_c_0, logic_block_1_c_1, logic_block_1_c_2,
       logic_block_1_c_3, logic_block_1_p_0, logic_block_1_p_1, logic_block_1_p_2, logic_block_1_p_3,
       n7_segment_display_2_p1, n7_segment_display_2_p3, n7_segment_display_3_p2, n7_segment_display_4_p1,
       n7_segment_display_4_p3, n7_segment_display_4_p4, n7_segment_display_5_p2, n7_segment_display_6_p1,
       n7_segment_display_7_p1, pg_generator_1_g0, pg_generator_1_g1, pg_generator_1_g2, pg_generator_1_g3,
       pg_generator_1_p0, pg_generator_1_p1, pg_generator_1_p2, pg_generator_1_p3;

  _7_Segment_Display u_7_segment_display_1 (.b(Cin), .c(Cin));  // open: g, f, a, e, d, dp
  // BCD_to_7_Segment_decoder bcd_to_7_segment_decoder_1: pin names not known; wires that end beside it: bcd_to_7_segment_decoder_1_p1, bcd_to_7_segment_decoder_1_p1, bcd_to_7_segment_decoder_1_p1
  // _7_Segment_Display 7_segment_display_2: pin names not known; wires that end beside it: n7_segment_display_2_p1, n7_segment_display_2_p1, n7_segment_display_2_p3
  // _7_Segment_Display 7_segment_display_3: pin names not known; wires that end beside it: bcd_to_7_segment_decoder_1_p1, n7_segment_display_3_p2, n7_segment_display_3_p2
  // BCD_to_7_Segment_decoder bcd_to_7_segment_decoder_2: pin names not known
  // Binairy_to_BCD_converter #(.binvalue(4)) binairy_to_bcd_converter_1: pin names not known; wires that end beside it: A
  PG_GENERATOR pg_generator_1 (
    .P1(pg_generator_1_p1), .P3(pg_generator_1_p3), .B1(B[1]), .B3(B[3]), .A1(A[1]), .A3(A[3]), .A2(A[2]),
    .A0(A[0]), .B2(B[2]), .B0(B[0]), .P2(pg_generator_1_p2), .P0(pg_generator_1_p0), .G3(pg_generator_1_g3),
    .G2(pg_generator_1_g2), .G1(pg_generator_1_g1), .G0(pg_generator_1_g0));
  // BCD_to_7_Segment_decoder bcd_to_7_segment_decoder_3: pin names not known; wires that end beside it: n7_segment_display_2_p3, n7_segment_display_2_p3
  // _7_Segment_Display 7_segment_display_4: pin names not known; wires that end beside it: n7_segment_display_4_p1, n7_segment_display_4_p1, n7_segment_display_4_p3, n7_segment_display_4_p4
  // _7_Segment_Display 7_segment_display_5: pin names not known; wires that end beside it: n7_segment_display_2_p3, n7_segment_display_5_p2, n7_segment_display_5_p2
  // BCD_to_7_Segment_decoder bcd_to_7_segment_decoder_4: pin names not known
  // Binairy_to_BCD_converter #(.binvalue(4)) binairy_to_bcd_converter_2: pin names not known; wires that end beside it: B
  LOGIC_BLOCK logic_block_1 (
    .c0(Cin), .p0(pg_generator_1_p0), .g0(pg_generator_1_g0), .p1(pg_generator_1_p1), .g1(pg_generator_1_g1),
    .p2(pg_generator_1_p2), .g2(pg_generator_1_g2), .p3(pg_generator_1_p3), .g3(pg_generator_1_g3),
    .c_0(logic_block_1_c_0), .p_0(logic_block_1_p_0), .c_1(logic_block_1_c_1), .p_1(logic_block_1_p_1),
    .c_2(logic_block_1_c_2), .p_2(logic_block_1_p_2), .c_3(logic_block_1_c_3), .p_3(logic_block_1_p_3),
    .c_4(Cout));
  // BCD_to_7_Segment_decoder bcd_to_7_segment_decoder_5: pin names not known; wires that end beside it: n7_segment_display_4_p3, n7_segment_display_4_p4
  // _7_Segment_Display 7_segment_display_6: pin names not known; wires that end beside it: n7_segment_display_6_p1, n7_segment_display_6_p1
  // Binairy_to_BCD_converter #(.binvalue(5)) binairy_to_bcd_converter_3: pin names not known; wires that end beside it: {Cout, S}
  ADDER_BLOCK adder_block_1 (
    .s0(S[0]), .p3(logic_block_1_p_3), .p2(logic_block_1_p_2), .p1(logic_block_1_p_1),
    .p0(logic_block_1_p_0), .c0(logic_block_1_c_0), .c1(logic_block_1_c_1), .c2(logic_block_1_c_2),
    .c3(logic_block_1_c_3), .s1(S[1]), .s2(S[2]), .s3(S[3]));
  // _7_Segment_Display 7_segment_display_7: pin names not known; wires that end beside it: n7_segment_display_7_p1, n7_segment_display_7_p1
  // BCD_to_7_Segment_decoder bcd_to_7_segment_decoder_6: pin names not known
endmodule

module LOGIC_BLOCK (
  input  c0,
  input  p0,
  input  g0,
  input  p1,
  input  g1,
  input  p2,
  input  g2,
  input  p3,
  input  g3,
  output c_0,
  output p_0,
  output c_1,
  output p_1,
  output c_2,
  output p_2,
  output c_3,
  output p_3,
  output c_4
);

  wire and_1_out, and_2_out, and_3_out, and_4_out, and_5_out, and_6_out, and_7_out, and_8_out, and_9_out,
       and_10_out;

  and and_1 (and_1_out, p3, p2, p1, p0, c0);
  and and_2 (and_2_out, p3, p2, p1, g0);
  and and_3 (and_3_out, p2, g1, p3);
  and and_4 (and_4_out, p3, g2);
  and and_5 (and_5_out, c0, p0, p1, p2);
  and and_6 (and_6_out, g0, p1, p2);
  and and_7 (and_7_out, g1, p2);
  and and_8 (and_8_out, c0, p0, p1);
  and and_9 (and_9_out, g0, p1);
  and and_10 (and_10_out, c0, p1);
  or or_1 (c_4, and_1_out, and_2_out, and_3_out, and_4_out, g3);
  or or_2 (c_3, and_5_out, and_6_out, and_7_out, g2);
  or or_3 (c_2, and_8_out, and_9_out, g1);
  or or_4 (c_1, and_10_out, g0);

  assign c_0 = c0;
  assign p_0 = p0;
  assign p_1 = p1;
  assign p_2 = p2;
  assign p_3 = p3;
endmodule

module PG_GENERATOR (
  input  A3,
  input  A2,
  input  A1,
  input  A0,
  input  B3,
  input  B2,
  input  B1,
  input  B0,
  output P3,
  output P2,
  output P1,
  output P0,
  output G3,
  output G2,
  output G1,
  output G0
);

  HA MSB (.A(A3), .P(P3), .B(B3), .G(G3));
  HA ha_1 (.A(A2), .P(P2), .B(B2), .G(G2));
  HA ha_2 (.A(A1), .P(P1), .B(B1), .G(G1));
  HA LSB (.A(A0), .P(P0), .B(B0), .G(G0));
endmodule

module ADDER_BLOCK (
  input  p0,
  input  c0,
  input  p1,
  input  c1,
  input  p2,
  input  c2,
  input  p3,
  input  c3,
  output s0,
  output s1,
  output s2,
  output s3
);

  xor xor_1 (s0, p0, c0);
  xor xor_2 (s1, p1, c1);
  xor xor_3 (s2, p2, c2);
  xor xor_4 (s3, p3, c3);
endmodule

module HA (
  input  A,
  input  B,
  output G,
  output P
);

  and and_1 (G, A, B);
  xor xor_1 (P, A, B);
endmodule
